// Logisim project Q1.circ as structural Verilog: 1 circuit, main circuit main
module main (
  input  in_1,
  input  in_2,
  input  in_3,
  input  in_4,
  output out_5,
  output out_6,
  output out_7,
  output out_8
);

  not not_1 (out_5, in_1);
  not not_2 (out_6, in_2);
  not not_3 (out_7, in_3);
  not not_4 (out_8, in_4);

  // Notes on the sheet:
  //   A3
  //   O3
  //   A2
  //   A1
  //   A0
  //   O2
  //   O1
  //   O0
endmodule
