// Logisim project Q2.circ as structural Verilog: 3 circuits, main circuit main
module main (
  input  in_1,
  input  in_2,
  input  in_3,
  input  in_4,
  output out_5,
  output out_6,
  output out_7,
  output out_8
);

  wire not_1_out, not_2_out, not_3_out, not_4_out, undriven;

  not not_1 (not_1_out, in_1);
  not not_2 (not_2_out, in_2);
  not not_3 (not_3_out, in_3);
  not not_4 (not_4_out, in_4);
  FOUR_BIT_ADDER four_bit_adder_1 (
    .A0(not_4_out), .A1(not_3_out), .A2(not_2_out), .A3(not_1_out), .B0(1'b1), .B1(undriven), .O3(out_5),
    .O2(out_6), .O1(out_7), .O0(out_8));  // open: B2, B3, S_OUT

  // Notes on the sheet:
  //   INPUT
  //   A3
  //   A2
  //   A1
  //   A0
  //   O3
  //   O2
  //   O1
  //   O0
  //   OUTPUT
endmodule

module FULLADDER (
  input  A,
  input  B,
  input  C_IN,
  output S,
  output C_OUT
);

  wire and_1_out, and_2_out, xor_1_out;

  and and_1 (and_1_out, A, B);
  xor xor_1 (xor_1_out, A, B);
  xor xor_2 (S, xor_1_out, C_IN);
  and and_2 (and_2_out, xor_1_out, C_IN);
  or or_1 (C_OUT, and_2_out, and_1_out);

  // Notes on the sheet:
  //   AXORB
endmodule

module FOUR_BIT_ADDER (
  input  A0,
  input  A1,
  input  A2,
  input  A3,
  input  B0,
  input  B1,
  input  B2,
  input  B3,
  output O3,
  output O2,
  output O1,
  output O0,
  output S_OUT
);

  wire fulladder_1_c_out, fulladder_2_c_out, fulladder_3_c_out;

  FULLADDER fulladder_1 (.A(A0), .B(B0), .C_IN(1'b0), .S(O0), .C_OUT(fulladder_1_c_out));
  FULLADDER fulladder_2 (.A(A1), .B(B1), .C_IN(fulladder_1_c_out), .S(O1), .C_OUT(fulladder_2_c_out));
  FULLADDER fulladder_3 (.A(A2), .B(B2), .C_IN(fulladder_2_c_out), .S(O2), .C_OUT(fulladder_3_c_out));
  FULLADDER fulladder_4 (.A(A3), .B(B3), .C_IN(fulladder_3_c_out), .S(O3), .C_OUT(S_OUT));
endmodule
