// Logisim project Q3.circ as structural Verilog: 2 circuits, main circuit main
module main (
  input  in_1,
  input  in_2,
  input  in_3,
  input  B0,
  input  A3,
  input  A2,
  input  A1,
  input  A0,
  output out_9,
  output out_10,
  output out_11,
  output out_12
);

  wire half_adder_1_c_out, half_adder_2_c_out, half_adder_2_s, half_adder_3_c_out, half_adder_4_c_out,
       half_adder_4_s, half_adder_5_c_out, half_adder_7_c_out, half_adder_7_s, or_1_out, or_2_out, or_3_out,
       or_4_out, or_5_out, or_6_out;

  or or_1 (or_1_out, out_12, half_adder_1_c_out);
  HALF_ADDER half_adder_1 (.A(A0), .S(out_12), .C_OUT(half_adder_1_c_out));  // open: B
  HALF_ADDER half_adder_2 (.A(or_1_out), .B(B0), .S(half_adder_2_s), .C_OUT(half_adder_2_c_out));
  or or_2 (or_2_out, half_adder_2_s, half_adder_2_c_out);
  HALF_ADDER half_adder_3 (.A(A1), .B(or_2_out), .S(out_11), .C_OUT(half_adder_3_c_out));
  or or_3 (or_3_out, out_11, half_adder_3_c_out);
  HALF_ADDER half_adder_4 (.A(or_3_out), .B(in_3), .S(half_adder_4_s), .C_OUT(half_adder_4_c_out));
  HALF_ADDER half_adder_5 (.A(A2), .B(or_4_out), .S(out_10), .C_OUT(half_adder_5_c_out));
  or or_4 (or_4_out, half_adder_4_s, half_adder_4_c_out);
  buf or_5 (or_5_out, out_9);  // OR_Gate
  HALF_ADDER half_adder_6 (.A(A3), .S(out_9));  // open: B, C_OUT
  HALF_ADDER half_adder_7 (.A(or_5_out), .S(half_adder_7_s), .C_OUT(half_adder_7_c_out));  // open: B
  or or_6 (or_6_out, half_adder_7_s, half_adder_7_c_out);
endmodule

module HALF_ADDER (
  input  A,
  input  B,
  output S,
  output C_OUT
);

  xor xor_1 (S, A, B);
  and and_1 (C_OUT, A, B);
endmodule
