// Logisim project q10_half_subtractor.circ as structural Verilog: 1 circuit, main circuit main
module main (
  input  A,
  input  B,
  output SUB,
  output BORROW
);

  wire not_1_out;

  not not_1 (not_1_out, A);
  xor xor_1 (SUB, A, B);
  and and_1 (BORROW, not_1_out, B);

  // Notes on the sheet:
  //   A-B
endmodule
