// Logisim project q11_full_subtractor.circ as structural Verilog: 1 circuit, main circuit main
module main (
  input  A,
  input  B,
  input  C_BORROW,
  output SUB,
  output BORROW
);

  wire and_1_out, and_2_out, and_3_out, not_1_out;

  not not_1 (not_1_out, A);
  ExactlyOne xor_1 (.out(SUB), .in0(A), .in1(B), .in2(C_BORROW));
  and and_1 (and_1_out, not_1_out, B);
  and and_2 (and_2_out, not_1_out, C_BORROW);
  and and_3 (and_3_out, B, C_BORROW);
  or or_1 (BORROW, and_1_out, and_2_out, and_3_out);

  // Notes on the sheet:
  //   A'
endmodule
