// Logisim project q13_bcd_subtractor.circ as structural Verilog: 3 circuits, main circuit main
module main (
  input  A3,
  input  A2,
  input  A1,
  input  A0,
  input  B3,
  input  B2,
  input  B1,
  input  B0,
  output BORROW,
  output S3,
  output S2,
  output S1,
  output S0
);

  wire four_bit_adder_1_carry, four_bit_adder_1_s0, four_bit_adder_1_s1, four_bit_adder_1_s2,
       four_bit_adder_1_s3, not_1_out, xor_1_out, xor_2_out, xor_3_out, xor_4_out, xor_5_out, xor_6_out,
       xor_7_out, xor_8_out;

  xor xor_1 (xor_1_out, B3, 1'b1);
  xor xor_2 (xor_2_out, B2, 1'b1);
  xor xor_3 (xor_3_out, B1, 1'b1);
  xor xor_4 (xor_4_out, B0, 1'b1);
  four_bit_adder four_bit_adder_1 (
    .A3(A3), .A2(A2), .A1(A1), .A0(A0), .B3(xor_1_out), .B2(xor_2_out), .B1(xor_3_out), .B0(xor_4_out),
    .CARRY_IN(1'b1), .CARRY(four_bit_adder_1_carry), .S3(four_bit_adder_1_s3), .S2(four_bit_adder_1_s2),
    .S1(four_bit_adder_1_s1), .S0(four_bit_adder_1_s0));
  not not_1 (not_1_out, four_bit_adder_1_carry);
  xor xor_5 (xor_5_out, four_bit_adder_1_s3, not_1_out);
  xor xor_6 (xor_6_out, four_bit_adder_1_s2, not_1_out);
  xor xor_7 (xor_7_out, four_bit_adder_1_s1, not_1_out);
  xor xor_8 (xor_8_out, four_bit_adder_1_s0, not_1_out);
  four_bit_adder four_bit_adder_2 (
    .A3(xor_5_out), .A2(xor_6_out), .A1(xor_7_out), .A0(xor_8_out), .CARRY_IN(not_1_out), .CARRY(BORROW),
    .S3(S3), .S2(S2), .S1(S1), .S0(S0));  // open: B3, B2, B1, B0
endmodule

module four_bit_adder (
  input  A3,
  input  A2,
  input  A1,
  input  A0,
  input  B3,
  input  B2,
  input  B1,
  input  B0,
  input  CARRY_IN,
  output CARRY,
  output S3,
  output S2,
  output S1,
  output S0
);

  wire full_adder_1_carry, full_adder_2_carry, full_adder_3_carry;

  full_adder full_adder_1 (.A(A0), .B(B0), .C(CARRY_IN), .SUM(S0), .CARRY(full_adder_1_carry));
  full_adder full_adder_2 (.A(A1), .B(B1), .C(full_adder_1_carry), .SUM(S1), .CARRY(full_adder_2_carry));
  full_adder full_adder_3 (.A(A2), .B(B2), .C(full_adder_2_carry), .SUM(S2), .CARRY(full_adder_3_carry));
  full_adder full_adder_4 (.A(A3), .B(B3), .C(full_adder_3_carry), .SUM(S3), .CARRY(CARRY));
endmodule

module full_adder (
  input  A,
  input  B,
  input  C,
  output SUM,
  output CARRY
);

  wire and_1_out, and_2_out, and_3_out;

  ExactlyOne xor_1 (.out(SUM), .in0(A), .in1(B), .in2(C));
  and and_1 (and_1_out, A, B);
  and and_2 (and_2_out, B, C);
  and and_3 (and_3_out, C, A);
  or or_1 (CARRY, and_1_out, and_2_out, and_3_out);
endmodule
