// Logisim project q14_4_bit_comparator.circ as structural Verilog
module main (
  input  A3,
  input  A2,
  input  A1,
  input  A0,
  input  B3,
  input  B2,
  input  B1,
  input  B0,
  output A_greater_than_B,
  output A_EQUAL_B,
  output A_less_than_B
);

  wire and_1_out, and_2_out, and_3_out, and_4_out, and_5_out, and_6_out, and_7_out, and_8_out, not_1_out,
       not_2_out, not_3_out, not_4_out, not_5_out, not_6_out, not_7_out, not_8_out, xnor_1_out, xnor_2_out,
       xnor_3_out, xnor_4_out;

  not not_1 (not_1_out, A1);
  not not_2 (not_2_out, A0);
  not not_3 (not_3_out, B3);
  not not_4 (not_4_out, B2);
  not not_5 (not_5_out, B1);
  not not_6 (not_6_out, B0);
  not not_7 (not_7_out, A2);
  and and_1 (and_1_out, A3, not_3_out);
  and and_2 (and_2_out, A2, not_4_out, xnor_1_out);
  and and_3 (and_3_out, A1, not_5_out, xnor_1_out, xnor_2_out);
  and and_4 (and_4_out, A0, not_6_out, xnor_1_out, xnor_3_out);
  not not_8 (not_8_out, A3);
  xnor xnor_1 (xnor_1_out, A3, B3);
  xnor xnor_2 (xnor_2_out, A2, B2);
  xnor xnor_3 (xnor_3_out, A1, B1);
  xnor xnor_4 (xnor_4_out, A0, B0);
  and and_5 (and_5_out, not_8_out, B3);
  and and_6 (and_6_out, not_7_out, B2, xnor_1_out);
  and and_7 (and_7_out, not_1_out, B1, xnor_1_out, xnor_2_out);
  and and_8 (and_8_out, not_2_out, B0, xnor_2_out, xnor_3_out);
  or or_1 (A_greater_than_B, and_1_out, and_2_out, and_3_out, and_4_out);
  and and_9 (A_EQUAL_B, xnor_1_out, xnor_2_out, xnor_3_out, xnor_4_out);
  or or_2 (A_less_than_B, and_5_out, and_6_out, and_7_out, and_8_out);

  // Notes on the sheet:
  //   A3
endmodule

module A_EQU_B (
  input  A3,
  input  A2,
  input  A1,
  input  A0,
  input  B3,
  input  B2,
  input  B1,
  input  B0,
  output A_EQUAL_B
);

  wire xnor_1_out, xnor_2_out, xnor_3_out, xnor_4_out;

  xnor xnor_1 (xnor_1_out, A3, B3);
  xnor xnor_2 (xnor_2_out, A2, B2);
  xnor xnor_3 (xnor_3_out, A1, B1);
  xnor xnor_4 (xnor_4_out, A0, B0);
  and and_1 (A_EQUAL_B, xnor_1_out, xnor_2_out, xnor_3_out, xnor_4_out);
endmodule
