// Logisim project q15_parity_bit_generator.circ as structural Verilog: 1 circuit, main circuit main
module main (
  input  A,
  input  B,
  input  C,
  input  A1,
  input  B1,
  input  C1,
  output EVEN_PARITY,
  output ODD_PARITY
);

  wire xor_1_out, xor_2_out, xor_4_out;

  xor xor_1 (xor_1_out, A, B);
  xor xor_2 (xor_2_out, A1, B1);
  xor xor_3 (EVEN_PARITY, xor_1_out, C);
  xor xor_4 (xor_4_out, xor_2_out, C1);
  not not_1 (ODD_PARITY, xor_4_out);
endmodule
