// Logisim project q5_half_adder.circ as structural Verilog: 1 circuit, main circuit main
module main (
  input  A,
  input  B,
  output sum,
  output carry
);

  xor xor_1 (sum, A, B);
  and and_1 (carry, A, B);
endmodule
