// Logisim project q6_full_adder.circ as structural Verilog: 1 circuit, main circuit main
module main (
  input  A,
  input  B,
  input  C,
  output S,
  output CARRY
);

  wire and_1_out, and_2_out, and_3_out;

  ExactlyOne xor_1 (.out(S), .in0(A), .in1(B), .in2(C));
  and and_1 (and_1_out, A, B);
  and and_2 (and_2_out, B, C);
  and and_3 (and_3_out, C, A);
  or or_1 (CARRY, and_1_out, and_2_out, and_3_out);
endmodule
