// Logisim project q8_4bit_adder_using_full_adder.circ as structural Verilog: 2 circuits, main circuit main
module main (
  input  A3,
  input  A2,
  input  A1,
  input  A0,
  input  B3,
  input  B2,
  input  B1,
  input  B0,
  output CARRY,
  output S3,
  output S2,
  output S1,
  output S0
);

  wire full_adder_1_carry, full_adder_2_carry, full_adder_3_carry;

  full_adder full_adder_1 (.A(A0), .B(B0), .C(1'b0), .SUM(S0), .CARRY(full_adder_1_carry));
  full_adder full_adder_2 (.A(A1), .B(B1), .C(full_adder_1_carry), .SUM(S1), .CARRY(full_adder_2_carry));
  full_adder full_adder_3 (.A(A2), .B(B2), .C(full_adder_2_carry), .SUM(S2), .CARRY(full_adder_3_carry));
  full_adder full_adder_4 (.A(A3), .B(B3), .C(full_adder_3_carry), .SUM(S3), .CARRY(CARRY));
endmodule

module full_adder (
  input  A,
  input  B,
  input  C,
  output SUM,
  output CARRY
);

  wire and_1_out, and_2_out, and_3_out;

  ExactlyOne xor_1 (.out(SUM), .in0(A), .in1(B), .in2(C));
  and and_1 (and_1_out, A, B);
  and and_2 (and_2_out, B, C);
  and and_3 (and_3_out, C, A);
  or or_1 (CARRY, and_1_out, and_2_out, and_3_out);
endmodule
