// Logisim project q9_4_bit_subtractor_using_4_bit_adder.circ as structural Verilog: 3 circuits, main circuit main
module main (
  input  B3,
  input  B2,
  input  B1,
  input  B0,
  input  A3,
  input  A2,
  input  A1,
  input  A0,
  input  in_9,
  output CARRY,
  output S3,
  output S2,
  output S1,
  output S0
);

  wire xor_1_out, xor_2_out, xor_3_out, xor_4_out;

  xor xor_1 (xor_1_out, in_9, B3);
  xor xor_2 (xor_2_out, in_9, B2);
  xor xor_3 (xor_3_out, in_9, B1);
  xor xor_4 (xor_4_out, in_9, B0);
  four_bit_adder four_bit_adder_1 (
    .A3(A3), .A2(A2), .A1(A1), .A0(A0), .B3(xor_1_out), .B2(xor_2_out), .B1(xor_3_out), .B0(xor_4_out),
    .CARRY_I(in_9), .CARRY(CARRY), .S3(S3), .S2(S2), .S1(S1), .S0(S0));

  // Notes on the sheet:
  //   A-B
endmodule

module full_adder (
  input  A,
  input  B,
  input  C_IN,
  output SUM,
  output CARRY
);

  wire and_1_out, and_2_out, and_3_out;

  ExactlyOne xor_1 (.out(SUM), .in0(A), .in1(B), .in2(C_IN));
  and and_1 (and_1_out, A, B);
  and and_2 (and_2_out, B, C_IN);
  and and_3 (and_3_out, C_IN, A);
  or or_1 (CARRY, and_1_out, and_2_out, and_3_out);
endmodule

module four_bit_adder (
  input  A3,
  input  A2,
  input  A1,
  input  A0,
  input  B3,
  input  B2,
  input  B1,
  input  B0,
  input  CARRY_I,
  output CARRY,
  output S3,
  output S2,
  output S1,
  output S0
);

  wire full_adder_1_carry, full_adder_2_carry, full_adder_3_carry;

  full_adder full_adder_1 (.A(A0), .B(B0), .C_IN(CARRY_I), .SUM(S0), .CARRY(full_adder_1_carry));
  full_adder full_adder_2 (.A(A1), .B(B1), .C_IN(full_adder_1_carry), .SUM(S1), .CARRY(full_adder_2_carry));
  full_adder full_adder_3 (.A(A2), .B(B2), .C_IN(full_adder_2_carry), .SUM(S2), .CARRY(full_adder_3_carry));
  full_adder full_adder_4 (.A(A3), .B(B3), .C_IN(full_adder_3_carry), .SUM(S3), .CARRY(CARRY));
endmodule
