// Logisim project 1s COMPLEMENT USING NOT GATE.circ as structural Verilog: 1 circuit, main circuit main
module main (
  input  D3,
  input  D2,
  input  D1,
  input  D0,
  input  A3,
  input  A2,
  input  A1,
  input  A0,
  input  MODE,
  output out_10,
  output out_11,
  output out_12,
  output out_13,
  output out_14,
  output out_15,
  output out_16,
  output out_17
);

  not not_1 (out_14, D3);
  not not_2 (out_15, D2);
  not not_3 (out_16, D1);
  not not_4 (out_17, D0);
  xor xor_1 (out_10, A3, MODE);
  xor xor_2 (out_11, A2, MODE);
  xor xor_3 (out_12, A1, MODE);
  xor xor_4 (out_13, A0, MODE);
endmodule
