// Logisim project 1s complement using XOR and XNOR.circ as structural Verilog: 1 circuit, main circuit main
module main (
  input  in_1,
  input  fixed_1,
  input  in_3,
  input  fixed_0,
  output out_5,
  output out_6
);

  xor xor_1 (out_5, in_1, fixed_1);
  xnor xnor_1 (out_6, in_3, fixed_0);

  // Notes on the sheet:
  //   1's complement using XOR
  //   1's complement using XNOR
endmodule
