// Logisim project 2's COMPLEMENT USING 4 BIT ADDER AND XOR GATE.circ as structural Verilog: 5 circuits, main circuit main
module main (
  input  mode1,
  input  A0,
  input  A1,
  input  A2,
  input  A3,
  input  logic0,
  output out_7,
  output out_8,
  output out_9,
  output out_10
);

  FourBitAdderSubtractor fourbitaddersubtractor_1 (
    .b3(A3), .a3(logic0), .b2(A2), .a2(logic0), .b1(A1), .a1(logic0), .b0(A0), .a0(logic0), .M(mode1),
    .s3(out_10), .s2(out_9), .s1(out_8), .s0(out_7));  // open: c4

  // Notes on the sheet:
  //   2's COMPLEMENT ( USING XOR AND 4 BIT ADDER - SUBTRACTOR)
endmodule

module full_adder_f2fdb414 (
  input  A,
  input  B,
  input  C,
  output SUM,
  output CARRY
);

  wire and_1_out, and_2_out, and_3_out;

  and and_1 (and_1_out, A, B);
  and and_2 (and_2_out, A, C);
  and and_3 (and_3_out, B, C);
  xor xor_1 (SUM, A, B, C);
  or or_1 (CARRY, and_1_out, and_2_out, and_3_out);
endmodule

module L_4_bit_adder_acd38e99 (
  input  a0,
  input  a1,
  input  a2,
  input  a3,
  input  b1,
  input  b2,
  input  b3,
  input  b0,
  input  c_in_42decffc,
  output s3,
  output s0,
  output s1,
  output s2,
  output c_out_284c8091
);

  wire full_adder_f2fdb414_1_carry, full_adder_f2fdb414_2_carry, full_adder_f2fdb414_3_carry;

  full_adder_f2fdb414 full_adder_f2fdb414_1 (
    .A(a0), .B(b0), .C(c_in_42decffc), .SUM(s0), .CARRY(full_adder_f2fdb414_1_carry));
  full_adder_f2fdb414 full_adder_f2fdb414_2 (
    .A(a1), .B(full_adder_f2fdb414_1_carry), .C(b1), .SUM(s1), .CARRY(full_adder_f2fdb414_2_carry));
  full_adder_f2fdb414 full_adder_f2fdb414_3 (
    .A(a2), .B(full_adder_f2fdb414_2_carry), .C(b2), .SUM(s2), .CARRY(full_adder_f2fdb414_3_carry));
  full_adder_f2fdb414 full_adder_f2fdb414_4 (
    .A(a3), .B(full_adder_f2fdb414_3_carry), .C(b3), .SUM(s3), .CARRY(c_out_284c8091));
endmodule

module FullAdder (
  input  ai,
  input  bi,
  input  cin,
  output sum,
  output carry
);

  wire and_1_out, and_2_out, and_3_out;

  and and_1 (and_1_out, ai, bi);
  and and_2 (and_2_out, ai, cin);
  and and_3 (and_3_out, bi, cin);
  xor xor_1 (sum, ai, bi, cin);
  or or_1 (carry, and_1_out, and_2_out, and_3_out);
endmodule

module FourBitAdderSubtractor (
  input  b3,
  input  a3,
  input  b2,
  input  a2,
  input  b1,
  input  a1,
  input  b0,
  input  a0,
  input  M,
  output c4,
  output s3,
  output s2,
  output s1,
  output s0
);

  wire fulladder_2_carry, fulladder_3_carry, fulladder_4_carry, xor_1_out, xor_2_out, xor_3_out, xor_4_out;

  xor xor_1 (xor_1_out, b3, M);
  FullAdder fulladder_1 (.ai(a3), .bi(xor_1_out), .cin(fulladder_2_carry), .sum(s3), .carry(c4));
  xor xor_2 (xor_2_out, b2, M);
  FullAdder fulladder_2 (.ai(a2), .bi(xor_2_out), .cin(fulladder_3_carry), .sum(s2), .carry(fulladder_2_carry));
  xor xor_3 (xor_3_out, b1, M);
  FullAdder fulladder_3 (.ai(a1), .bi(xor_3_out), .cin(fulladder_4_carry), .sum(s1), .carry(fulladder_3_carry));
  xor xor_4 (xor_4_out, b0, M);
  FullAdder fulladder_4 (.ai(a0), .bi(xor_4_out), .cin(M), .sum(s0), .carry(fulladder_4_carry));
endmodule
