// Logisim project 2_BIT_COMPARATOR.circ as structural Verilog: 1 circuit, main circuit main
module main (
  input  A1,
  input  B1,
  input  A0,
  input  B0,
  output A_greaterThan_B,
  output A_equals_B,
  output A_lessThan_B
);

  wire and_1_out, and_2_out, and_3_out, and_4_out, not_1_out, not_2_out, not_3_out, not_4_out, xnor_1_out,
       xnor_2_out;

  not not_1 (not_1_out, B1);
  not not_2 (not_2_out, B0);
  not not_3 (not_3_out, A0);
  not not_4 (not_4_out, A1);
  xnor xnor_1 (xnor_1_out, A1, B1);
  xnor xnor_2 (xnor_2_out, A0, B0);
  and and_1 (and_1_out, A1, not_1_out);
  and and_2 (and_2_out, A0, not_2_out, xnor_1_out);
  and and_3 (and_3_out, xnor_1_out, B0, not_3_out);
  and and_4 (and_4_out, B1, not_4_out);
  or or_1 (A_greaterThan_B, and_1_out, and_2_out);
  and and_5 (A_equals_B, xnor_1_out, xnor_2_out);
  or or_2 (A_lessThan_B, and_3_out, and_4_out);

  // Notes on the sheet:
  //   2 BIT COMPARATOR
endmodule
