// Logisim project 2sComplementUsingFourBitAdder.circ as structural Verilog: 3 circuits, main circuit main
module main (
  input  D3,
  input  D0,
  input  D1,
  input  D2,
  input  M,
  input  \logic ,
  output out_7,
  output out_8,
  output out_9,
  output out_10
);

  wire xor_1_out, xor_2_out, xor_3_out, xor_4_out;

  xor xor_1 (xor_1_out, D0, M);
  xor xor_2 (xor_2_out, D1, M);
  FourBitAdder fourbitadder_1 (
    .b3(\logic ), .a3(xor_4_out), .b2(\logic ), .a2(xor_3_out), .b1(\logic ), .a1(xor_2_out), .cin(M),
    .b0(\logic ), .a0(xor_1_out), .s3(out_10), .s2(out_9), .s1(out_8), .s0(out_7));  // open: carry
  xor xor_3 (xor_3_out, D2, M);
  xor xor_4 (xor_4_out, D3, M);

  // Notes on the sheet:
  //   2's Complement using 4 bit Adder
endmodule

module FourBitAdder (
  input  b3,
  input  a3,
  input  b2,
  input  a2,
  input  b1,
  input  a1,
  input  cin,
  input  b0,
  input  a0,
  output carry,
  output s3,
  output s2,
  output s1,
  output s0
);

  wire fulladder_2_carry, fulladder_3_carry, fulladder_4_carry;

  FullAdder fulladder_1 (.ai(a3), .bi(b3), .cin(fulladder_2_carry), .sum(s3), .carry(carry));
  FullAdder fulladder_2 (.ai(a2), .bi(b2), .cin(fulladder_3_carry), .sum(s2), .carry(fulladder_2_carry));
  FullAdder fulladder_3 (.ai(a1), .bi(b1), .cin(fulladder_4_carry), .sum(s1), .carry(fulladder_3_carry));
  FullAdder fulladder_4 (.ai(a0), .bi(b0), .cin(cin), .sum(s0), .carry(fulladder_4_carry));
endmodule

module FullAdder (
  input  ai,
  input  bi,
  input  cin,
  output sum,
  output carry
);

  wire and_1_out, and_2_out, and_3_out;

  and and_1 (and_1_out, ai, bi);
  and and_2 (and_2_out, ai, cin);
  and and_3 (and_3_out, bi, cin);
  xor xor_1 (sum, ai, bi, cin);
  or or_1 (carry, and_1_out, and_2_out, and_3_out);
endmodule
