// Logisim project 8_BIT_ADDER_USING_4_BIT_CLA.circ as structural Verilog: 2 circuits, main circuit main
module main (
  input  Logic_0,
  input  a0,
  input  b0,
  input  a1,
  input  b1,
  input  a2,
  input  b2,
  input  a3,
  input  b3,
  input  a4,
  input  b4,
  input  a5,
  input  b5,
  input  a6,
  input  b6,
  input  a7,
  input  b7,
  output S0,
  output S1,
  output S2,
  output S3,
  output S4,
  output S5,
  output S6,
  output S7
);

  wire four_bit_cla_1_c3;

  Four_Bit_Cla four_bit_cla_1 (
    .Cin(Logic_0), .A0(a0), .B0(b0), .A1(a1), .B1(b1), .A2(a2), .B2(b2), .A3(a3), .B3(b3), .s0(S0), .s1(S1),
    .s2(S2), .s3(S3), .C3(four_bit_cla_1_c3));  // open: C0, C1, C2
  Four_Bit_Cla four_bit_cla_2 (
    .Cin(four_bit_cla_1_c3), .A0(a4), .B0(b4), .A1(a5), .B1(b5), .A2(a6), .B2(b6), .A3(a7), .B3(b7), .s0(S4),
    .s1(S5), .s2(S6), .s3(S7));  // open: C0, C1, C2, C3
endmodule

module Four_Bit_Cla (
  input  Cin,
  input  A0,
  input  B0,
  input  A1,
  input  B1,
  input  A2,
  input  B2,
  input  A3,
  input  B3,
  output s0,
  output C0,
  output s1,
  output C1,
  output s2,
  output C2,
  output s3,
  output C3
);

  wire and_1_out, and_2_out, and_3_out, and_4_out, and_5_out, and_6_out, and_7_out, Gi_out, Pi_out,
       xor_1_out, xor_2_out, xor_3_out;

  and Gi (Gi_out, A0, B0);
  xor Pi (Pi_out, A0, B0);
  and and_1 (and_1_out, A1, B1);
  xor xor_1 (xor_1_out, A1, B1);
  and and_2 (and_2_out, A2, B2);
  xor xor_2 (xor_2_out, A2, B2);
  and and_3 (and_3_out, A3, B3);
  xor xor_3 (xor_3_out, A3, B3);
  and and_4 (and_4_out, Cin, Pi_out);
  and and_5 (and_5_out, C0, xor_1_out);
  and and_6 (and_6_out, C1, xor_2_out);
  and and_7 (and_7_out, C2, xor_3_out);
  or or_1 (C0, Gi_out, and_4_out);
  or or_2 (C1, and_1_out, and_5_out);
  or or_3 (C2, and_2_out, and_6_out);
  or or_4 (C3, and_3_out, and_7_out);
  xor xor_4 (s0, Cin, Pi_out);
  xor xor_5 (s1, C0, xor_1_out);
  xor xor_6 (s2, C1, xor_2_out);
  xor xor_7 (s3, C2, xor_3_out);
endmodule
