// Logisim project FOUR_BITS_ALU_USING_FOUR_ONE_MUX.circ as structural Verilog: 3 circuits, main circuit main
module main (
  input  A3,
  input  A2,
  input  A1,
  input  A0,
  input  B3,
  input  B2,
  input  B1,
  input  B0,
  input  MODE_0,
  input  MODE_1,
  input  [1:0] S1S0,
  output out_12,
  output [3:0] Y_OUT,
  output out_14
);

  wire [3:0] adder_subtractor_1_s0, adder_subtractor_2_s0, and_1_out, or_1_out;

  assign and_1_out = {B3, B2, B1, B0} & {A3, A2, A1, A0};  // AND_Gate and_1, 4 bits wide
  assign or_1_out = {B3, B2, B1, B0} | {A3, A2, A1, A0};  // OR_Gate or_1, 4 bits wide
  ADDER_SUBTRACTOR adder_subtractor_1 (
    .b3(B3), .a3(A3), .b2(B2), .a2(A2), .b1(B1), .a1(A1), .b0(B0), .a0(A0), .M(MODE_0), .c4(out_12),
    .s3(adder_subtractor_1_s0[3]), .s2(adder_subtractor_1_s0[2]), .s1(adder_subtractor_1_s0[1]),
    .s0(adder_subtractor_1_s0[0]));
  ADDER_SUBTRACTOR adder_subtractor_2 (
    .b3(B3), .a3(A3), .b2(B2), .a2(A2), .b1(B1), .a1(A1), .b0(B0), .a0(A0), .M(MODE_1), .c4(out_14),
    .s3(adder_subtractor_2_s0[3]), .s2(adder_subtractor_2_s0[2]), .s1(adder_subtractor_2_s0[1]),
    .s0(adder_subtractor_2_s0[0]));
  Multiplexer #(.select(2), .width(4)) multiplexer_1 (
    .in0(adder_subtractor_1_s0), .in1(adder_subtractor_2_s0), .in2(and_1_out), .in3(or_1_out), .out(Y_OUT),
    .sel(S1S0));
endmodule

module ADDER_SUBTRACTOR (
  input  b3,
  input  a3,
  input  b2,
  input  a2,
  input  b1,
  input  a1,
  input  b0,
  input  a0,
  input  M,
  output c4,
  output s3,
  output s2,
  output s1,
  output s0
);

  wire full_adder_2_carry, full_adder_3_carry, full_adder_4_carry, xor_1_out, xor_2_out, xor_3_out, xor_4_out;

  xor xor_1 (xor_1_out, b3, M);
  FULL_ADDER full_adder_1 (.ai(a3), .bi(xor_1_out), .cin(full_adder_2_carry), .sum(s3), .carry(c4));
  xor xor_2 (xor_2_out, b2, M);
  FULL_ADDER full_adder_2 (.ai(a2), .bi(xor_2_out), .cin(full_adder_3_carry), .sum(s2), .carry(full_adder_2_carry));
  xor xor_3 (xor_3_out, b1, M);
  FULL_ADDER full_adder_3 (.ai(a1), .bi(xor_3_out), .cin(full_adder_4_carry), .sum(s1), .carry(full_adder_3_carry));
  xor xor_4 (xor_4_out, b0, M);
  FULL_ADDER full_adder_4 (.ai(a0), .bi(xor_4_out), .cin(M), .sum(s0), .carry(full_adder_4_carry));
endmodule

module FULL_ADDER (
  input  ai,
  input  bi,
  input  cin,
  output sum,
  output carry
);

  wire and_1_out, and_2_out, and_3_out, xor_1_out;

  xor xor_1 (xor_1_out, ai, bi);
  and and_1 (and_1_out, ai, bi);
  and and_2 (and_2_out, ai, cin);
  and and_3 (and_3_out, bi, cin);
  xor xor_2 (sum, xor_1_out, cin);
  or or_1 (carry, and_1_out, and_2_out, and_3_out);
endmodule
