// Logisim project Left_Shift_Register.circ as structural Verilog: 1 circuit, main circuit main
module main (
  input  i3,
  input  i2,
  input  i1,
  input  i0,
  input  in_5,
  input  in_6,
  output y3,
  output y2,
  output y1,
  output y0
);

  Multiplexer #(.select(2)) multiplexer_1 (.in0(i3), .in1(i2), .in2(i1), .in3(i0), .out(y3), .sel({in_6, in_5}));
  Multiplexer #(.select(2)) multiplexer_2 (.in0(i2), .in1(i1), .in2(i0), .in3(i3), .out(y2), .sel({in_6, in_5}));
  Multiplexer #(.select(2)) multiplexer_3 (.in0(i1), .in1(i0), .in2(i3), .in3(i2), .out(y1), .sel({in_6, in_5}));
  Multiplexer #(.select(2)) multiplexer_4 (.in0(i0), .in1(i3), .in2(i2), .in3(i1), .out(y0), .sel({in_6, in_5}));
endmodule
