// Logisim project Random_synchronous_counter.circ as structural Verilog: 1 circuit, main circuit main
module main (
);

  wire and_1_out, clock_1_out, or_1_out, or_2_out, t_ff_1_q, t_ff_1_qn, t_ff_2_q, t_ff_2_qn, t_ff_3_q;

  Clock clock_1 (.out(clock_1_out));
  T_Flip_Flop #(.trigger("falling")) t_ff_1 (
    .T(t_ff_2_q), .clk(clock_1_out), .Q(t_ff_1_q), .Qn(t_ff_1_qn));  // open: reset, preset
  or or_1 (or_1_out, t_ff_2_q, t_ff_1_q, t_ff_3_q);
  T_Flip_Flop #(.trigger("falling")) t_ff_2 (
    .T(or_1_out), .clk(clock_1_out), .Q(t_ff_2_q), .Qn(t_ff_2_qn));  // open: reset, preset
  and and_1 (and_1_out, t_ff_1_qn, t_ff_2_qn);
  T_Flip_Flop #(.trigger("falling")) t_ff_3 (.T(or_2_out), .clk(clock_1_out), .Q(t_ff_3_q));  // open: Qn, reset, preset
  or or_2 (or_2_out, t_ff_3_q, and_1_out);

  // Notes on the sheet:
  //   T_a
  //   T_b
  //   T_c
endmodule
