// Logisim project SIXTEEN_BITS_SHIFTER.circ as structural Verilog: 2 circuits, main circuit main
module main (
  input  in_1,
  input  in_2,
  input  in_3,
  input  in_4,
  input  in_5,
  input  in_6,
  input  in_7,
  input  in_8,
  input  in_9,
  input  in_10,
  input  in_11,
  input  in_12,
  input  in_13,
  input  in_14,
  input  in_15,
  input  in_16,
  input  [1:0] in_17
);

  Left_shift_register left_shift_register_1 (
    .i3(in_8), .i2(in_7), .i1(in_6), .i0(in_5), .i_minus1(in_17[0]), .i_minus2(in_17[1]));  // open: i_minus3, s0, s1, y3, y2, y1, y0
  Left_shift_register left_shift_register_2 (
    .i3(in_4), .i2(in_3), .i1(in_2), .i0(in_1), .i_minus1(in_17[0]), .i_minus2(in_17[1]));  // open: i_minus3, s0, s1, y3, y2, y1, y0
  Left_shift_register left_shift_register_3 (
    .i3(in_12), .i2(in_11), .i1(in_10), .i0(in_9), .i_minus1(in_17[0]), .i_minus2(in_17[1]));  // open: i_minus3, s0, s1, y3, y2, y1, y0
  Left_shift_register left_shift_register_4 (
    .i3(in_16), .i2(in_15), .i1(in_14), .i0(in_13), .i_minus1(in_17[0]), .i_minus2(in_17[1]));  // open: i_minus3, s0, s1, y3, y2, y1, y0
endmodule

module Left_shift_register (
  input  i3,
  input  i2,
  input  i1,
  input  i0,
  input  i_minus1,
  input  i_minus2,
  input  i_minus3,
  input  s0,
  input  s1,
  output y3,
  output y2,
  output y1,
  output y0
);

  Multiplexer #(.select(2)) multiplexer_1 (.in0(i3), .in1(i2), .in2(i1), .in3(i0), .out(y3), .sel({s1, s0}));
  Multiplexer #(.select(2)) multiplexer_2 (.in0(i2), .in1(i1), .in2(i0), .in3(i_minus1), .out(y2), .sel({s1, s0}));
  Multiplexer #(.select(2)) multiplexer_3 (
    .in0(i1), .in1(i0), .in2(i_minus1), .in3(i_minus2), .out(y1), .sel({s1, s0}));
  Multiplexer #(.select(2)) multiplexer_4 (
    .in0(i0), .in1(i_minus1), .in2(i_minus2), .in3(i_minus3), .out(y0), .sel({s1, s0}));
endmodule
