// Logisim project ALU_EIGHT_OPERATIONS.circ as structural Verilog: 3 circuits, main circuit main
module main (
  input  [3:0] A,
  input  [3:0] B,
  input  in_3
);

  FOUR_BIT_ADDER_SUBTRACTOR four_bit_adder_subtractor_1 (
    .b3(B[3]), .a3(A[3]), .b2(B[2]), .a2(A[2]), .b1(B[1]), .a1(A[1]), .b0(B[0]), .a0(A[0]), .M(in_3));  // open: c4, s3, s2, s1, s0
  FOUR_BIT_ADDER_SUBTRACTOR four_bit_adder_subtractor_2 (
    .b3(B[3]), .a3(B[3]), .b2(B[2]), .a2(A[2]), .b1(B[1]), .a1(A[1]), .b0(B[0]), .a0(A[0]));  // open: M, c4, s3, s2, s1, s0
  FOUR_BIT_ADDER_SUBTRACTOR four_bit_adder_subtractor_3 (
    .b3(B[3]), .b2(B[2]), .b1(B[1]), .b0(B[0]));  // open: a3, a2, a1, a0, M, c4, s3, s2, s1, s0
  FOUR_BIT_ADDER_SUBTRACTOR four_bit_adder_subtractor_4 ();  // open: b3, a3, b2, a2, b1, a1, b0, a0, M, c4, s3, s2, s1, s0
endmodule

module FOUR_BIT_ADDER_SUBTRACTOR (
  input  b3,
  input  a3,
  input  b2,
  input  a2,
  input  b1,
  input  a1,
  input  b0,
  input  a0,
  input  M,
  output c4,
  output s3,
  output s2,
  output s1,
  output s0
);

  wire full_adder_2_carry, full_adder_3_carry, full_adder_4_carry, xor_1_out, xor_2_out, xor_3_out, xor_4_out;

  xor xor_1 (xor_1_out, b3, M);
  FULL_ADDER full_adder_1 (.ai(a3), .bi(xor_1_out), .cin(full_adder_2_carry), .sum(s3), .carry(c4));
  xor xor_2 (xor_2_out, b2, M);
  FULL_ADDER full_adder_2 (.ai(a2), .bi(xor_2_out), .cin(full_adder_3_carry), .sum(s2), .carry(full_adder_2_carry));
  xor xor_3 (xor_3_out, b1, M);
  FULL_ADDER full_adder_3 (.ai(a1), .bi(xor_3_out), .cin(full_adder_4_carry), .sum(s1), .carry(full_adder_3_carry));
  xor xor_4 (xor_4_out, b0, M);
  FULL_ADDER full_adder_4 (.ai(a0), .bi(xor_4_out), .cin(M), .sum(s0), .carry(full_adder_4_carry));
endmodule

module FULL_ADDER (
  input  ai,
  input  bi,
  input  cin,
  output sum,
  output carry
);

  wire and_1_out, and_2_out, and_3_out, xor_1_out;

  xor xor_1 (xor_1_out, ai, bi);
  and and_1 (and_1_out, ai, bi);
  and and_2 (and_2_out, ai, cin);
  and and_3 (and_3_out, bi, cin);
  xor xor_2 (sum, xor_1_out, cin);
  or or_1 (carry, and_1_out, and_2_out, and_3_out);
endmodule
