// Logisim project RANDOM_SEQUENCE_GENERATOR.circ as structural Verilog: 1 circuit, main circuit main
module main (
);

  wire A_q, A_qn, and_1_out, and_2_out, and_3_out, and_4_out, and_5_out, B_q, B_qn, C_q, C_qn, clock_1_out,
       or_1_out;

  Clock clock_1 (.out(clock_1_out));
  T_Flip_Flop #(.trigger("falling")) A (.T(and_1_out), .clk(clock_1_out), .Q(A_q), .Qn(A_qn));  // open: reset, preset
  and and_1 (and_1_out, C_qn, B_q);
  and and_2 (and_2_out, B_q, C_qn);
  and and_3 (and_3_out, C_qn, A_q);
  T_Flip_Flop #(.trigger("falling")) B (.T(or_1_out), .clk(clock_1_out), .Q(B_q), .Qn(B_qn));  // open: reset, preset
  or or_1 (or_1_out, and_2_out, and_3_out, and_4_out);
  and and_4 (and_4_out, and_5_out, C_q);
  T_Flip_Flop #(.trigger("falling")) C (.T(and_5_out), .clk(clock_1_out), .Q(C_q), .Qn(C_qn));  // open: reset, preset
  and and_5 (and_5_out, A_qn, B_qn);

  // Notes on the sheet:
  //   LSB
  //   MSB
endmodule
