// Logisim project BCD_Adder.circ as structural Verilog: 3 circuits, main circuit main
module main (
  input  a0,
  input  b0,
  input  a1,
  input  b1,
  input  a2,
  input  b2,
  input  a3,
  input  b3,
  input  cin,
  input  \logic ,
  output S0,
  output S1,
  output S2,
  output S3,
  output C
);

  wire and_1_out, and_2_out, fourbitadder_2_carry, fourbitadder_2_s0, fourbitadder_2_s1, fourbitadder_2_s2,
       fourbitadder_2_s3;

  FourBitAdder fourbitadder_1 (
    .b3(fourbitadder_2_s3), .a3(\logic ), .b2(fourbitadder_2_s2), .a2(C), .b1(fourbitadder_2_s1), .a1(C),
    .cin(cin), .b0(fourbitadder_2_s0), .a0(\logic ), .s3(S3), .s2(S2), .s1(S1), .s0(S0));  // open: carry
  FourBitAdder fourbitadder_2 (
    .b3(b3), .a3(a3), .b2(b2), .a2(a2), .b1(b1), .a1(a1), .cin(cin), .b0(b0), .a0(a0),
    .carry(fourbitadder_2_carry), .s3(fourbitadder_2_s3), .s2(fourbitadder_2_s2), .s1(fourbitadder_2_s1),
    .s0(fourbitadder_2_s0));
  and and_1 (and_1_out, fourbitadder_2_s3, fourbitadder_2_s2);
  and and_2 (and_2_out, fourbitadder_2_s3, fourbitadder_2_s1);
  or or_1 (C, fourbitadder_2_carry, and_1_out, and_2_out);

  // Notes on the sheet:
  //   BCD ADDER
endmodule

module FullAdder (
  input  ai,
  input  bi,
  input  cin,
  output sum,
  output carry
);

  wire and_1_out, and_2_out, and_3_out, xor_1_out;

  xor xor_1 (xor_1_out, ai, bi);
  and and_1 (and_1_out, ai, bi);
  and and_2 (and_2_out, ai, cin);
  and and_3 (and_3_out, bi, cin);
  xor xor_2 (sum, xor_1_out, cin);
  or or_1 (carry, and_1_out, and_2_out, and_3_out);
endmodule

module FourBitAdder (
  input  b3,
  input  a3,
  input  b2,
  input  a2,
  input  b1,
  input  a1,
  input  cin,
  input  b0,
  input  a0,
  output carry,
  output s3,
  output s2,
  output s1,
  output s0
);

  wire fulladder_2_carry, fulladder_3_carry, fulladder_4_carry;

  FullAdder fulladder_1 (.ai(a3), .bi(b3), .cin(fulladder_2_carry), .sum(s3), .carry(carry));
  FullAdder fulladder_2 (.ai(a2), .bi(b2), .cin(fulladder_3_carry), .sum(s2), .carry(fulladder_2_carry));
  FullAdder fulladder_3 (.ai(a1), .bi(b1), .cin(fulladder_4_carry), .sum(s1), .carry(fulladder_3_carry));
  FullAdder fulladder_4 (.ai(a0), .bi(b0), .cin(cin), .sum(s0), .carry(fulladder_4_carry));
endmodule
