// Logisim project FULL ADDER1.circ as structural Verilog: 1 circuit, main circuit main
module main (
  input  ai,
  input  bi,
  input  cin,
  output sum,
  output carry
);

  wire and_1_out, and_2_out, and_3_out;

  and and_1 (and_1_out, ai, bi);
  and and_2 (and_2_out, ai, cin);
  and and_3 (and_3_out, bi, cin);
  xor xor_1 (sum, ai, bi, cin);
  or or_1 (carry, and_1_out, and_2_out, and_3_out);

  // Notes on the sheet:
  //   FULL ADDER
endmodule
