// Logisim project FourBitAdder.circ as structural Verilog: 2 circuits, main circuit main
module main (
  input  b3,
  input  a3,
  input  b2,
  input  a2,
  input  b1,
  input  a1,
  input  cin,
  input  b0,
  input  a0,
  output carry,
  output s3,
  output s2,
  output s1,
  output s0
);

  wire fulladder_2_carry, fulladder_3_carry, fulladder_4_carry;

  fulladder fulladder_1 (.ai(a3), .bi(b3), .cin(fulladder_2_carry), .sum(s3), .carry(carry));
  fulladder fulladder_2 (.ai(a2), .bi(b2), .cin(fulladder_3_carry), .sum(s2), .carry(fulladder_2_carry));
  fulladder fulladder_3 (.ai(a1), .bi(b1), .cin(fulladder_4_carry), .sum(s1), .carry(fulladder_3_carry));
  fulladder fulladder_4 (.ai(a0), .bi(b0), .cin(cin), .sum(s0), .carry(fulladder_4_carry));

  // Notes on the sheet:
  //   FOUR BIT ADDER
endmodule

module fulladder (
  input  ai,
  input  bi,
  input  cin,
  output sum,
  output carry
);

  wire and_1_out, and_2_out, and_3_out, xor_1_out;

  xor xor_1 (xor_1_out, ai, bi);
  and and_1 (and_1_out, ai, bi);
  and and_2 (and_2_out, ai, cin);
  and and_3 (and_3_out, bi, cin);
  xor xor_2 (sum, xor_1_out, cin);
  or or_1 (carry, and_1_out, and_2_out, and_3_out);
endmodule
