// Logisim project FourBitAdder_Subtractor.circ as structural Verilog: 2 circuits, main circuit main
module main (
  input  b3,
  input  a3,
  input  b2,
  input  a2,
  input  b1,
  input  a1,
  input  b0,
  input  a0,
  input  M,
  output c4,
  output s3,
  output s2,
  output s1,
  output s0
);

  wire fulladder_2_carry, fulladder_3_carry, fulladder_4_carry, xor_1_out, xor_2_out, xor_3_out, xor_4_out;

  xor xor_1 (xor_1_out, b3, M);
  FullAdder fulladder_1 (.ai(a3), .bi(xor_1_out), .cin(fulladder_2_carry), .sum(s3), .carry(c4));
  xor xor_2 (xor_2_out, b2, M);
  FullAdder fulladder_2 (.ai(a2), .bi(xor_2_out), .cin(fulladder_3_carry), .sum(s2), .carry(fulladder_2_carry));
  xor xor_3 (xor_3_out, b1, M);
  FullAdder fulladder_3 (.ai(a1), .bi(xor_3_out), .cin(fulladder_4_carry), .sum(s1), .carry(fulladder_3_carry));
  xor xor_4 (xor_4_out, b0, M);
  FullAdder fulladder_4 (.ai(a0), .bi(xor_4_out), .cin(M), .sum(s0), .carry(fulladder_4_carry));
endmodule

module FullAdder (
  input  ai,
  input  bi,
  input  cin,
  output sum,
  output carry
);

  wire and_1_out, and_2_out, and_3_out, xor_1_out;

  xor xor_1 (xor_1_out, ai, bi);
  and and_1 (and_1_out, ai, bi);
  and and_2 (and_2_out, ai, cin);
  and and_3 (and_3_out, bi, cin);
  xor xor_2 (sum, xor_1_out, cin);
  or or_1 (carry, and_1_out, and_2_out, and_3_out);
endmodule
