// Logisim project FullSubtractor.circ as structural Verilog: 1 circuit, main circuit main
module main (
  input  a,
  input  b,
  input  bin,
  input  A1,
  input  B1,
  output diff,
  output out_7,
  output out_8,
  output borrow
);

  wire and_2_out, and_3_out, and_4_out, not_1_out, not_2_out;

  not not_1 (not_1_out, A1);
  xor xor_1 (out_7, A1, B1);
  and and_1 (out_8, not_1_out, B1);
  not not_2 (not_2_out, a);
  and and_2 (and_2_out, bin, not_2_out);
  and and_3 (and_3_out, not_2_out, b);
  and and_4 (and_4_out, bin, b);
  xor xor_2 (diff, a, b, bin);
  or or_1 (borrow, and_2_out, and_3_out, and_4_out);

  // Notes on the sheet:
  //   FULL SUBTRACTOR
endmodule
