// Logisim project HALF ADDER.circ as structural Verilog: 1 circuit, main circuit main
module main (
  input  A,
  input  A_2,
  input  B,
  input  B_2,
  input  C,
  output out_6,
  output SUM,
  output out_8,
  output out_9
);

  wire and_2_out, and_3_out, and_4_out;

  xor xor_1 (out_6, A, B_2);
  and and_1 (out_8, A, B_2);
  and and_2 (and_2_out, A_2, B);
  and and_3 (and_3_out, A_2, C);
  and and_4 (and_4_out, B, C);
  xor xor_2 (SUM, A_2, B, C);
  or or_1 (out_9, and_2_out, and_3_out, and_4_out);

  // Notes on the sheet:
  //   FULL ADDER
  //   CARRY
endmodule
