// Logisim project TenComplementOfTwoDigitsBCD.circ as structural Verilog: 3 circuits, main circuit main
module main (
  input  D7,
  input  in_2,
  input  D6,
  input  in_4,
  input  D5,
  input  in_6,
  input  D4,
  input  in_8,
  input  in_9,
  input  in_10,
  input  D3,
  input  in_12,
  input  in_13,
  input  D2,
  input  in_15,
  input  D1,
  input  in_17,
  input  D0,
  input  in_19,
  input  in_20,
  input  in_21,
  input  in_22,
  output out_23,
  output out_24,
  output out_25,
  output out_26,
  output out_27,
  output out_28,
  output out_29,
  output out_30
);

  wire fourbitaddersubtractor_2_s0, fourbitaddersubtractor_2_s1, fourbitaddersubtractor_2_s2,
       fourbitaddersubtractor_2_s3;

  FourBitAdderSubtractor fourbitaddersubtractor_1 (
    .b3(D7), .a3(in_2), .b2(D6), .a2(in_4), .b1(D5), .a1(in_6), .b0(D4), .a0(in_8), .M(in_9), .s3(out_23),
    .s2(out_24), .s1(out_25), .s0(out_26));  // open: c4
  FourBitAdderSubtractor fourbitaddersubtractor_2 (
    .b3(D3), .a3(in_13), .b2(D2), .a2(in_15), .b1(D1), .a1(in_17), .b0(D0), .a0(in_20), .M(in_21),
    .s3(fourbitaddersubtractor_2_s3), .s2(fourbitaddersubtractor_2_s2), .s1(fourbitaddersubtractor_2_s1),
    .s0(fourbitaddersubtractor_2_s0));  // open: c4
  FourBitAdderSubtractor fourbitaddersubtractor_3 (
    .b3(in_10), .a3(fourbitaddersubtractor_2_s3), .b2(in_10), .a2(fourbitaddersubtractor_2_s2), .b1(in_10),
    .a1(fourbitaddersubtractor_2_s1), .b0(in_19), .a0(fourbitaddersubtractor_2_s0), .M(in_22), .s3(out_27),
    .s2(out_28), .s1(out_29), .s0(out_30));  // open: c4

  // Notes on the sheet:
  //   10's Complement of a Two digits BCD
  //   To complete the circuit, we need to add a bcd adder.. for the lower bytes
endmodule

module FullAdder (
  input  ai,
  input  bi,
  input  cin,
  output sum,
  output carry
);

  wire and_1_out, and_2_out, and_3_out, xor_1_out;

  xor xor_1 (xor_1_out, ai, bi);
  and and_1 (and_1_out, ai, bi);
  and and_2 (and_2_out, ai, cin);
  and and_3 (and_3_out, bi, cin);
  xor xor_2 (sum, xor_1_out, cin);
  or or_1 (carry, and_1_out, and_2_out, and_3_out);
endmodule

module FourBitAdderSubtractor (
  input  b3,
  input  a3,
  input  b2,
  input  a2,
  input  b1,
  input  a1,
  input  b0,
  input  a0,
  input  M,
  output c4,
  output s3,
  output s2,
  output s1,
  output s0
);

  wire fulladder_2_carry, fulladder_3_carry, fulladder_4_carry, xor_1_out, xor_2_out, xor_3_out, xor_4_out;

  xor xor_1 (xor_1_out, b3, M);
  FullAdder fulladder_1 (.ai(a3), .bi(xor_1_out), .cin(fulladder_2_carry), .sum(s3), .carry(c4));
  xor xor_2 (xor_2_out, b2, M);
  FullAdder fulladder_2 (.ai(a2), .bi(xor_2_out), .cin(fulladder_3_carry), .sum(s2), .carry(fulladder_2_carry));
  xor xor_3 (xor_3_out, b1, M);
  FullAdder fulladder_3 (.ai(a1), .bi(xor_3_out), .cin(fulladder_4_carry), .sum(s1), .carry(fulladder_3_carry));
  xor xor_4 (xor_4_out, b0, M);
  FullAdder fulladder_4 (.ai(a0), .bi(xor_4_out), .cin(M), .sum(s0), .carry(fulladder_4_carry));
endmodule
