// Logisim project Q2.circ as structural Verilog: 2 circuits, main circuit main
module main (
  input  C1,
  input  C0,
  input  B,
  input  A,
  output out_5
);

  wire and_1_out, xor_1_out;

  xor xor_1 (xor_1_out, A, B);
  and and_1 (and_1_out, A, B);
  mux mux_1 (.s1(C1), .s0(C0), .I0(xor_1_out), .I1(xor_1_out), .I2(and_1_out), .I3(and_1_out), .O(out_5));

  // Notes on the sheet:
  //   LSB
endmodule

module mux (
  input  s1,
  input  s0,
  input  I0,
  input  I1,
  input  I2,
  input  I3,
  output O
);

  wire and_1_out, and_2_out, and_3_out, and_4_out, not_1_out, not_2_out;

  not not_1 (not_1_out, s0);
  not not_2 (not_2_out, s1);
  and and_1 (and_1_out, not_1_out, not_2_out, I0);
  and and_2 (and_2_out, not_2_out, s0, I1);
  and and_3 (and_3_out, s1, not_1_out, I2);
  and and_4 (and_4_out, s1, s0, I3);
  or or_1 (O, and_1_out, and_2_out, and_3_out, and_4_out);

  // Notes on the sheet:
  //   s0
  //   s1
endmodule
