// Logisim project q1.circ as structural Verilog: 4 circuits, main circuit main
module main (
  output out_1,
  output out_2,
  output out_3,
  output out_4
);

  wire and_1_out, and_2_out, and_3_out, and_4_out, and_5_out, clock_1_out, not_1_out, or_1_out;

  Clock clock_1 (.out(clock_1_out));
  and and_1 (and_1_out, out_2, out_3, out_4);
  or or_1 (or_1_out, out_2, out_4);
  J_K_Flip_Flop #(.trigger("falling")) j_k_ff_1 (
    .J(and_1_out), .K(or_1_out), .clk(clock_1_out), .Q(out_1));  // open: Qn, preset, reset
  not not_1 (not_1_out, out_1);
  and and_2 (and_2_out, not_1_out, out_3, out_4);
  J_K_Flip_Flop #(.trigger("falling")) j_k_ff_2 (
    .J(and_2_out), .K(and_3_out), .clk(clock_1_out), .Q(out_2));  // open: Qn, preset, reset
  and and_3 (and_3_out, out_3, out_4);
  and and_4 (and_4_out, not_1_out, out_4);
  J_K_Flip_Flop #(.trigger("falling")) j_k_ff_3 (
    .J(and_4_out), .K(and_5_out), .clk(clock_1_out), .Q(out_3));  // open: Qn, preset, reset
  and and_5 (and_5_out, out_2, out_4);
  J_K_Flip_Flop #(.trigger("falling")) j_k_ff_4 (
    .J(1'b1), .K(1'b1), .clk(clock_1_out), .Q(out_4));  // open: Qn, preset, reset

  // Notes on the sheet:
  //   1
  //   2
  //   3
  //   4
endmodule

module segment (
  input  in_1,
  input  [3:0] in_2
);

  wire and_1_out, decoder_1_out0, decoder_1_out1, decoder_1_out2, decoder_1_out3, not_1_out, not_2_out,
       or_1_out, xor_1_out;

  Decoder #(.select(4)) decoder_1 (
    .out0(decoder_1_out0), .out1(decoder_1_out1), .out2(decoder_1_out2), .out3(decoder_1_out3), .sel(in_2),
    .en(in_1));  // open: out4, out5, out6, out7, out8, out9, out10, out11, out12, out13, out14, out15
  xor xor_1 (xor_1_out, decoder_1_out0, decoder_1_out2);
  and and_1 (and_1_out, decoder_1_out1, decoder_1_out0);
  not not_1 (not_1_out, decoder_1_out1);
  not not_2 (not_2_out, and_1_out);
  _7_Segment_Display u_7_segment_display_1 (.a(xor_1_out), .b(or_1_out));  // open: g, f, e, d, c, dp
  or or_1 (or_1_out, and_1_out, decoder_1_out3, not_1_out, not_2_out);

  // Notes on the sheet:
  //   b1.b0
endmodule

module a (
  input  b0,
  input  b1,
  input  b2,
  input  b3,
  output fa,
  output fb,
  output fc,
  output fd,
  output fe,
  output ff,
  output fg
);

  wire and_1_out, and_2_out, and_3_out, and_4_out, and_5_out, and_6_out, and_7_out, and_8_out, and_9_out,
       and_10_out, and_11_out, not_1_out, not_2_out, not_3_out, not_4_out, not_5_out, not_6_out, not_7_out,
       not_8_out, not_9_out, not_10_out, or_4_out;

  not not_1 (not_1_out, b2);
  not not_2 (not_2_out, b0);
  not not_3 (not_3_out, b2);
  not not_4 (not_4_out, b0);
  not not_5 (not_5_out, b1);
  not not_6 (not_6_out, b0);
  not not_7 (not_7_out, b1);
  and and_1 (and_1_out, b1, not_2_out);
  and and_2 (and_2_out, b1, b0);
  and and_3 (and_3_out, b1, not_6_out);
  and and_4 (and_4_out, not_1_out, b1);
  and and_5 (and_5_out, not_7_out, b0, b2);
  and and_6 (and_6_out, not_3_out, not_2_out);
  xnor xnor_1 (fa, b0, b2);
  and and_7 (and_7_out, not_9_out, not_10_out);
  not not_8 (not_8_out, b2);
  not not_9 (not_9_out, b1);
  or or_1 (fc, b3, b2, not_5_out, b0);
  and and_8 (and_8_out, b2, not_7_out);
  and and_9 (and_9_out, b2, not_2_out);
  and and_10 (and_10_out, not_7_out, not_2_out);
  and and_11 (and_11_out, b1, not_4_out);
  not not_10 (not_10_out, b0);
  or or_2 (fe, and_1_out, and_6_out);
  or or_3 (fb, b3, and_2_out, not_8_out, and_7_out);
  or or_4 (or_4_out, b3, and_3_out, and_4_out, and_5_out);
  or or_5 (ff, b3, and_8_out, and_9_out, and_10_out);
  or or_6 (fg, b3, and_11_out);

  assign fd = b3;

  // Notes on the sheet:
  //   b0
  //   b1
  //   b2
endmodule

module b (
  input  in_1,
  input  in_2,
  input  in_3,
  input  in_4,
  input  in_5
);

  wire a_1_fa, a_1_fb, a_1_fc, a_1_fd, a_1_fe, a_1_ff, a_1_fg;

  _7_Segment_Display u_7_segment_display_1 ();  // open: g, f, a, b, e, d, c, dp
  a a_1 (
    .b0(in_2), .b1(in_3), .b2(in_4), .b3(in_5), .fa(a_1_fa), .fb(a_1_fb), .fc(a_1_fc), .fd(a_1_fd),
    .fe(a_1_fe), .ff(a_1_ff), .fg(a_1_fg));
  _7_Segment_Display u_7_segment_display_2 (
    .g(a_1_fg), .f(a_1_ff), .a(a_1_fa), .b(a_1_fb), .e(a_1_fe), .d(a_1_fd), .c(a_1_fc));  // open: dp
endmodule
