// Logisim project q2_sync_up_down_mod_8_counter.circ as structural Verilog: 1 circuit, main circuit main
module main (
  input  in_1,
  output A2,
  output A1,
  output A0
);

  wire and_1_out, and_2_out, and_3_out, and_4_out, clock_1_out, not_1_out, or_1_out, or_2_out, t_ff_1_qn,
       t_ff_2_qn;

  Clock #(.highDuration(2)) clock_1 (.out(clock_1_out));
  not not_1 (not_1_out, in_1);
  T_Flip_Flop t_ff_1 (.T(1'b1), .clk(clock_1_out), .Q(A0), .Qn(t_ff_1_qn));  // open: reset, preset
  and and_1 (and_1_out, A0, not_1_out);
  and and_2 (and_2_out, in_1, t_ff_1_qn);
  or or_1 (or_1_out, and_1_out, and_2_out);
  T_Flip_Flop t_ff_2 (.T(or_1_out), .clk(clock_1_out), .Q(A1), .Qn(t_ff_2_qn));  // open: reset, preset
  and and_3 (and_3_out, A1, and_1_out);
  and and_4 (and_4_out, and_2_out, t_ff_2_qn);
  or or_2 (or_2_out, and_3_out, and_4_out);
  T_Flip_Flop t_ff_3 (.T(or_2_out), .clk(clock_1_out), .Q(A2));  // open: Qn, reset, preset
endmodule
