// Logisim project q4_mod_8_up_down_counter_asyncronous.circ as structural Verilog: 1 circuit, main circuit main
module main (
  input  M,
  output A2,
  output A1,
  output A0
);

  wire and_1_out, and_2_out, and_3_out, and_4_out, clock_1_out, j_k_ff_1_qn, j_k_ff_2_qn, not_1_out,
       or_1_out, or_2_out;

  Clock clock_1 (.out(clock_1_out));
  not not_1 (not_1_out, M);
  J_K_Flip_Flop #(.trigger("falling")) j_k_ff_1 (
    .J(1'b1), .K(1'b1), .clk(clock_1_out), .Q(A0), .Qn(j_k_ff_1_qn));  // open: preset, reset
  and and_1 (and_1_out, A0, M);
  and and_2 (and_2_out, not_1_out, j_k_ff_1_qn);
  or or_1 (or_1_out, and_1_out, and_2_out);
  J_K_Flip_Flop #(.trigger("falling")) j_k_ff_2 (
    .J(1'b1), .K(1'b1), .clk(or_1_out), .Q(A1), .Qn(j_k_ff_2_qn));  // open: preset, reset
  and and_3 (and_3_out, A1, M);
  and and_4 (and_4_out, not_1_out, j_k_ff_2_qn);
  or or_2 (or_2_out, and_3_out, and_4_out);
  J_K_Flip_Flop #(.trigger("falling")) j_k_ff_3 (
    .J(1'b1), .K(1'b1), .clk(or_2_out), .Q(A2));  // open: Qn, preset, reset

  // Notes on the sheet:
  //   M=1 FOR THE UP COUNTER
  //   M=0 FOR THE DOWN COUNTER
endmodule
