// Logisim project q1.circ as structural Verilog: 6 circuits, main circuit main
module main (
  input  [3:0] a,
  input  [3:0] b,
  input  [1:0] s,
  output carray_borrow,
  output [3:0] O
);

  alu alu_1 (.a(a), .b(b), .s(s), .carry_borrow(carray_borrow), .op(O));
endmodule

module addition (
  input  [3:0] A,
  input  [3:0] B,
  output [3:0] sum_out,
  output c_out
);

  Adder #(.width(4)) adder_1 (.a(A), .b(B), .out(sum_out), .cout(c_out));  // open: cin
endmodule

module alu (
  input  [3:0] a,
  input  [3:0] b,
  input  [1:0] s,
  output carry_borrow,
  output [3:0] op
);

  wire subtraction_1_b_out;
  wire [3:0] addition_1_sum_out, nan_1_nan_d, subtraction_1_sub, x_or_1_xo;

  addition addition_1 (.A(a), .B(b), .sum_out(addition_1_sum_out), .c_out(carry_borrow));
  subtraction subtraction_1 (.A(a), .B(b), .sub(subtraction_1_sub), .b_out(subtraction_1_b_out));
  X_or x_or_1 (.A(a), .B(b), .xo(x_or_1_xo));
  nan nan_1 (.A(a), .B(b), .nan_d(nan_1_nan_d));
  Multiplexer #(.select(2), .width(4)) multiplexer_1 (
    .in0(addition_1_sum_out), .in1(subtraction_1_sub), .in2(x_or_1_xo), .in3(nan_1_nan_d), .out(op), .sel(s));
endmodule

module subtraction (
  input  [3:0] A,
  input  [3:0] B,
  output [3:0] sub,
  output b_out
);

  Subtractor #(.width(4)) subtractor_1 (.a(A), .b(B), .out(sub), .bout(b_out));  // open: bin
endmodule

module X_or (
  input  [3:0] A,
  input  [3:0] B,
  output [3:0] xo
);

  assign xo = A ^ B;  // XOR_Gate xor_1, 4 bits wide
endmodule

module nan (
  input  [3:0] A,
  input  [3:0] B,
  output [3:0] nan_d
);

  assign nan_d = ~(A & B);  // NAND_Gate nand_1, 4 bits wide
endmodule
